// Digital circuit register-file.dig as structural Verilog
module register_file (
  input  [4:0] ReadReg1,
  input  [4:0] ReadReg2,
  input  [4:0] WriteReg,
  input  [31:0] WriteData,
  input  RegWrite,
  input  Clock,
  output [31:0] ReadData1,
  output [31:0] ReadData2
);

  wire and_1_out, and_2_out, and_3_out, and_4_out, and_5_out, and_6_out, and_7_out, and_8_out, and_9_out,
       and_10_out, and_11_out, and_12_out, and_13_out, and_14_out, and_15_out, and_16_out, and_17_out,
       and_18_out, and_19_out, and_20_out, and_21_out, and_22_out, and_23_out, and_24_out, and_25_out,
       and_26_out, and_27_out, and_28_out, and_29_out, and_30_out, and_31_out, r1, r2, r3, r4, r5, r6, r7,
       r8, r9, r10, r11, r12, r13, r14, r15, r16, r17, r18, r19, r20, r21, r22, r23, r24, r25, r26, r27, r28,
       r29, r30, r31;
  wire [31:0] r1_q, r2_q, r3_q, r4_q, r5_q, r6_q, r7_q, r8_q, r9_q, r10_q, r11_q, r12_q, r13_q, r14_q, r15_q,
       r16_q, r17_q, r18_q, r19_q, r20_q, r21_q, r22_q, r23_q, r24_q, r25_q, r26_q, r27_q, r28_q, r29_q,
       r30_q, r31_q;

  Decoder #(.Selector_Bits(5)) decoder_1 (
    .sel(WriteReg), .out_1(r1), .out_2(r2), .out_3(r3), .out_4(r4), .out_5(r5), .out_6(r6), .out_7(r7),
    .out_8(r8), .out_9(r9), .out_10(r10), .out_11(r11), .out_12(r12), .out_13(r13), .out_14(r14),
    .out_15(r15), .out_16(r16), .out_17(r17), .out_18(r18), .out_19(r19), .out_20(r20), .out_21(r21),
    .out_22(r22), .out_23(r23), .out_24(r24), .out_25(r25), .out_26(r26), .out_27(r27), .out_28(r28),
    .out_29(r29), .out_30(r30), .out_31(r31));  // open: out_0
  and and_1 (and_1_out, r1, RegWrite);
  and and_2 (and_2_out, r5, RegWrite);
  and and_3 (and_3_out, r9, RegWrite);
  and and_4 (and_4_out, r13, RegWrite);
  and and_5 (and_5_out, r17, RegWrite);
  and and_6 (and_6_out, r21, RegWrite);
  and and_7 (and_7_out, r25, RegWrite);
  and and_8 (and_8_out, r29, RegWrite);
  Register #(.Bits(32)) u_R1 (.D(WriteData), .C(Clock), .en(and_1_out), .Q(r1_q));
  Register #(.Bits(32)) u_R5 (.D(WriteData), .C(Clock), .en(and_2_out), .Q(r5_q));
  Register #(.Bits(32)) u_R9 (.D(WriteData), .C(Clock), .en(and_3_out), .Q(r9_q));
  Register #(.Bits(32)) u_R13 (.D(WriteData), .C(Clock), .en(and_4_out), .Q(r13_q));
  Register #(.Bits(32)) u_R17 (.D(WriteData), .C(Clock), .en(and_5_out), .Q(r17_q));
  Register #(.Bits(32)) u_R21 (.D(WriteData), .C(Clock), .en(and_6_out), .Q(r21_q));
  Register #(.Bits(32)) u_R25 (.D(WriteData), .C(Clock), .en(and_7_out), .Q(r25_q));
  Register #(.Bits(32)) u_R29 (.D(WriteData), .C(Clock), .en(and_8_out), .Q(r29_q));
  and and_9 (and_9_out, r2, RegWrite);
  and and_10 (and_10_out, r6, RegWrite);
  and and_11 (and_11_out, r10, RegWrite);
  and and_12 (and_12_out, r14, RegWrite);
  and and_13 (and_13_out, r18, RegWrite);
  and and_14 (and_14_out, r22, RegWrite);
  and and_15 (and_15_out, r26, RegWrite);
  and and_16 (and_16_out, r30, RegWrite);
  Register #(.Bits(32)) u_R2 (.D(WriteData), .C(Clock), .en(and_9_out), .Q(r2_q));
  Register #(.Bits(32)) u_R6 (.D(WriteData), .C(Clock), .en(and_10_out), .Q(r6_q));
  Register #(.Bits(32)) u_R10 (.D(WriteData), .C(Clock), .en(and_11_out), .Q(r10_q));
  Register #(.Bits(32)) u_R14 (.D(WriteData), .C(Clock), .en(and_12_out), .Q(r14_q));
  Register #(.Bits(32)) u_R18 (.D(WriteData), .C(Clock), .en(and_13_out), .Q(r18_q));
  Register #(.Bits(32)) u_R22 (.D(WriteData), .C(Clock), .en(and_14_out), .Q(r22_q));
  Register #(.Bits(32)) u_R26 (.D(WriteData), .C(Clock), .en(and_15_out), .Q(r26_q));
  Register #(.Bits(32)) u_R30 (.D(WriteData), .C(Clock), .en(and_16_out), .Q(r30_q));
  and and_17 (and_17_out, r3, RegWrite);
  and and_18 (and_18_out, r7, RegWrite);
  and and_19 (and_19_out, r11, RegWrite);
  and and_20 (and_20_out, r15, RegWrite);
  and and_21 (and_21_out, r19, RegWrite);
  and and_22 (and_22_out, r23, RegWrite);
  and and_23 (and_23_out, r27, RegWrite);
  and and_24 (and_24_out, r31, RegWrite);
  Register #(.Bits(32)) u_R3 (.D(WriteData), .C(Clock), .en(and_17_out), .Q(r3_q));
  Register #(.Bits(32)) u_R7 (.D(WriteData), .C(Clock), .en(and_18_out), .Q(r7_q));
  Register #(.Bits(32)) u_R11 (.D(WriteData), .C(Clock), .en(and_19_out), .Q(r11_q));
  Register #(.Bits(32)) u_R15 (.D(WriteData), .C(Clock), .en(and_20_out), .Q(r15_q));
  Register #(.Bits(32)) u_R19 (.D(WriteData), .C(Clock), .en(and_21_out), .Q(r19_q));
  Register #(.Bits(32)) u_R23 (.D(WriteData), .C(Clock), .en(and_22_out), .Q(r23_q));
  Register #(.Bits(32)) u_R27 (.D(WriteData), .C(Clock), .en(and_23_out), .Q(r27_q));
  Register #(.Bits(32)) u_R31 (.D(WriteData), .C(Clock), .en(and_24_out), .Q(r31_q));
  and and_25 (and_25_out, r4, RegWrite);
  and and_26 (and_26_out, r8, RegWrite);
  and and_27 (and_27_out, r12, RegWrite);
  and and_28 (and_28_out, r16, RegWrite);
  and and_29 (and_29_out, r20, RegWrite);
  and and_30 (and_30_out, r24, RegWrite);
  and and_31 (and_31_out, r28, RegWrite);
  Register #(.Bits(32)) u_R4 (.D(WriteData), .C(Clock), .en(and_25_out), .Q(r4_q));
  Register #(.Bits(32)) u_R8 (.D(WriteData), .C(Clock), .en(and_26_out), .Q(r8_q));
  Register #(.Bits(32)) u_R12 (.D(WriteData), .C(Clock), .en(and_27_out), .Q(r12_q));
  Register #(.Bits(32)) u_R16 (.D(WriteData), .C(Clock), .en(and_28_out), .Q(r16_q));
  Register #(.Bits(32)) u_R20 (.D(WriteData), .C(Clock), .en(and_29_out), .Q(r20_q));
  Register #(.Bits(32)) u_R24 (.D(WriteData), .C(Clock), .en(and_30_out), .Q(r24_q));
  Register #(.Bits(32)) u_R28 (.D(WriteData), .C(Clock), .en(and_31_out), .Q(r28_q));
  Multiplexer #(.Selector_Bits(5), .Bits(32)) multiplexer_1 (
    .sel(ReadReg1), .in_0({32{1'b0}}), .in_1(r1_q), .in_2(r2_q), .in_3(r3_q), .in_4(r4_q), .in_5(r5_q),
    .in_6(r6_q), .in_7(r7_q), .in_8(r8_q), .in_9(r9_q), .in_10(r10_q), .in_11(r11_q), .in_12(r12_q),
    .in_13(r13_q), .in_14(r14_q), .in_15(r15_q), .in_16(r16_q), .in_17(r17_q), .in_18(r18_q), .in_19(r19_q),
    .in_20(r20_q), .in_21(r21_q), .in_22(r22_q), .in_23(r23_q), .in_24(r24_q), .in_25(r25_q), .in_26(r26_q),
    .in_27(r27_q), .in_28(r28_q), .in_29(r29_q), .in_30(r30_q), .in_31(r31_q), .out(ReadData1));
  Multiplexer #(.Selector_Bits(5), .Bits(32)) multiplexer_2 (
    .sel(ReadReg2), .in_0({32{1'b0}}), .in_1(r1_q), .in_2(r2_q), .in_3(r3_q), .in_4(r4_q), .in_5(r5_q),
    .in_6(r6_q), .in_7(r7_q), .in_8(r8_q), .in_9(r9_q), .in_10(r10_q), .in_11(r11_q), .in_12(r12_q),
    .in_13(r13_q), .in_14(r14_q), .in_15(r15_q), .in_16(r16_q), .in_17(r17_q), .in_18(r18_q), .in_19(r19_q),
    .in_20(r20_q), .in_21(r21_q), .in_22(r22_q), .in_23(r23_q), .in_24(r24_q), .in_25(r25_q), .in_26(r26_q),
    .in_27(r27_q), .in_28(r28_q), .in_29(r29_q), .in_30(r30_q), .in_31(r31_q), .out(ReadData2));

  // Other names for the same wires on the sheet: C = Clock
endmodule

/* Test case Register File Test:
WriteReg WriteData RegWrite Clock ReadReg1 ReadReg2 ReadData1 ReadData2

# $1 = 25
1 25 1 C 1 0 25 0

# $2 = 30
2 30 1 C 0 2 0 30

# $(N+1) = (N+1)
loop(N, 30)
	(N+1) (N+1) 1 C (N+1) (N) (N+1) (N)
end loop

# $(N+1) = N-60
loop(N, 30)
	(N+1) (N-60) 1 C (N+1) (N+1) (N-60) (N-60)
end loop

# Try writing to $0. This should not write anything
0 25 1 C 0 0 0 0

# try writing when RegWrite = 0
# (the registers should still have their old values)
loop(N, 30)
	(N+1) (N+80) 0 C (N+1) (N+1) (N-60) (N-60)
end loop
*/
