// Digital circuit boolean-unit.dig as structural Verilog
module boolean_unit (
  input  [31:0] A,
  input  [31:0] B,
  input  [1:0] Bool,
  output [31:0] Out
);

  wire [31:0] _1, _2, _3, _4;

  Multiplexer #(.Bits(32), .Selector_Bits(2)) multiplexer_1 (
    .sel(Bool), .in_0(_1), .in_1(_2), .in_2(_3), .in_3(_4), .out(Out));
  assign _1 = B & A;  // And and_1, 32 bits wide
  assign _2 = B | A;  // Or or_1, 32 bits wide
  assign _3 = B ^ A;  // XOr xor_1, 32 bits wide
  assign _4 = ~(B | A);  // NOr nor_1, 32 bits wide
endmodule

/* Test case Boolean Unit Test:
A B Bool Out
0xdcd84709 0x768a5af3 0 0x54884201
0x3d2cd361 0xf53106ef 0 0x35200261
0x28f56e63 0x854b7d0b 0 0x00416c03
0x9201A3De 0x2D1A9F88 1 0xBF1BBFDe
0xd15a7517 0xb900f275 1 0xf95af777
0xd81daa93 0x0ab5e9f7 1 0xdabdebf7
0x0f9eda3f 0x885e0a47 2 0x87c0d078
0xca58eed8 0x514af1fa 2 0x9b121f22
0xc7100004 0x3553ef1e 2 0xf243ef1a
0xd9537eed 0x133929ec 3 0x24848012
0x66b776e8 0xb2aa434b 3 0x09408814
0x745d1dab 0xafc46d88 3 0x00228254
*/
