// Digital circuit shifter.dig as structural Verilog
module shifter (
  input  [31:0] A,
  input  [31:0] B,
  input  [1:0] Bool,
  output [31:0] Out
);

  wire [31:0] S_LL, S_RA, S_RL;

  BarrelShifter #(.Bits(32)) Left_Logic (.in(B), .shift(A[5:0]), .out(S_LL));
  BarrelShifter #(.Bits(32), .direction("right")) Right_Logic (.in(B), .shift(A[5:0]), .out(S_RL));
  BarrelShifter #(.barrelShifterMode("arithmetic"), .Bits(32), .direction("right")) Right_Arithmetic (
    .in(B), .shift(A[5:0]), .out(S_RA));
  Multiplexer #(.Bits(32), .Selector_Bits(2)) multiplexer_1 (
    .sel(Bool), .in_0(S_LL), .in_1({32{1'b0}}), .in_2(S_RL), .in_3(S_RA), .out(Out));

  // Other names for the same wires on the sheet: A_t[5:0] = A[5:0]; C[25:0] = A[31:6]
endmodule

/* Test case Bidirectional Shifter Test:
A B Bool Out
0x43927735 0x310e576d    0 0x00000000
0x20693682 0x85050a62    0 0x14142988
0x737a6607 0x00b80c2b    0 0x5c061580
0x3629b085 0xe3088aeb    1 0x00000000
0x8403f72b 0xdc5ece59    1 0x00000000
0xae0824c7 0xbe187159    1 0x00000000
0xcb126889 0x0614e24a    2 0x00030a71
0x02352d86 0x54891132    2 0x01522444
0x00000001 0xF0000000    2 0x78000000
0xf77f1486 0x18e2f036    2 0x00638bc0
0x289a9211 0x6d349ef7    3 0x0000369a
0x3b9a2707 0xe9349ed3    3 0xffd2693d
0x22853218 0xd175490b    3 0xffffffd1
*/
